// Logisim project w1 실습.circ as structural Verilog: 1 circuit, main circuit main
module main (
  input  X,
  input  Y,
  input  A,
  input  B,
  input  Cin,
  output X_prime_Y_XY_prime,
  output S,
  output Cout
);

  wire and_1_out, and_2_out, and_3_out, and_4_out, not_1_out, not_2_out, xor_1_out, xor_2_out;

  not not_1 (not_1_out, Y);
  not not_2 (not_2_out, X);
  and and_1 (and_1_out, X, not_1_out);
  and and_2 (and_2_out, not_2_out, Y);
  xor xor_1 (xor_1_out, A, B);
  and and_3 (and_3_out, A, B);
  xor xor_2 (xor_2_out, A, B);
  or or_1 (X_prime_Y_XY_prime, and_1_out, and_2_out);
  and and_4 (and_4_out, xor_2_out, Cin);
  xor xor_3 (S, xor_1_out, Cin);
  or or_2 (Cout, and_3_out, and_4_out);
endmodule
