// Logisim project 로지심 기본 사용법.circ as structural Verilog: 1 circuit, main circuit main
module main (
  input  A,
  input  B,
  input  in_3,
  input  in_4,
  output A_prime_B,
  output A_B
);

  wire A_prime_out;

  not A_prime (A_prime_out, A);
  and and_1 (A_prime_B, A_prime_out, B);
  or or_1 (A_B, in_3, in_4);
  // XOR_Gate xor_1 is placed but not wired
endmodule
